// Logisim project sagui.circ as structural Verilog: 6 circuits, main circuit main
module main (
);

  wire clk, cntrlHL, comparator_1_eq, load, muxRaR0, muxUlaRam, store, wb, we;
  wire [1:0] multiplexer_3_out;
  wire [2:0] muxPc, ULA;
  wire [3:0] Imm;
  wire [7:0] BranchOnZero, BranchOnZeroImm, multiplexer_1_out, multiplexer_2_out, multiplexer_6_out, pc, PC1,
       pcImm, Ra, ram_1_dout, Rb, ula_1_s;
  wire [7:4] memInst_data;

  Adder adder_1 (.a(8'h1), .b(pc), .out(PC1));  // open: cin, cout
  Register register_1 (.D(multiplexer_1_out), .clk(clk), .Q(pc));  // open: en, clr
  Multiplexer #(.select(3), .width(8)) multiplexer_1 (
    .in0(PC1), .in1(Rb), .in2(pcImm), .in3(BranchOnZero), .in4(BranchOnZeroImm), .out(multiplexer_1_out),
    .sel(muxPc));  // open: in5, in6, in7
  Clock clock_1 (.out(clk));
  Adder adder_2 (.a(pc), .b({4'b0000, Imm}), .out(pcImm));  // open: cin, cout
  ROM memInst (.addr(pc), .data({memInst_data, Imm}));
  Multiplexer #(.width(8)) multiplexer_2 (.in0(multiplexer_6_out), .in1(Rb), .out(multiplexer_2_out), .sel(wb));
  Multiplexer #(.width(2)) multiplexer_3 (.in0(Imm[1:0]), .in1(2'b00), .out(multiplexer_3_out), .sel(muxRaR0));
  ROM #(.addrWidth(4), .dataWidth(13)) memControl (
    .addr(memInst_data), .data({cntrlHL, muxRaR0, muxUlaRam, load, store, we, wb, ULA, muxPc}));
  bankReg bankreg_1 (
    .WB(multiplexer_2_out), .WE(we), .ra(multiplexer_3_out), .rb(Imm[3:2]), .clk(clk), .out_6(Ra), .out_7(Rb));
  Multiplexer #(.width(8)) multiplexer_4 (.in0(PC1), .in1(Rb), .out(BranchOnZero), .sel(comparator_1_eq));
  Comparator comparator_1 (.a(Ra), .b({8{1'b0}}), .eq(comparator_1_eq));  // open: gt, lt
  ula ula_1 (.a(Ra), .b(Rb), .sel(ULA), .Imm(Imm), .CntrHL(cntrlHL), .s(ula_1_s));
  Multiplexer #(.width(8)) multiplexer_5 (.in0(PC1), .in1(pcImm), .out(BranchOnZeroImm), .sel(comparator_1_eq));
  RAM ram_1 (.addr(Rb), .we(store), .oe(load), .clk(clk), .din(Ra), .dout(ram_1_dout));
  Multiplexer #(.width(8)) multiplexer_6 (.in0(ula_1_s), .in1(ram_1_dout), .out(multiplexer_6_out), .sel(muxUlaRam));

  // Notes on the sheet:
  //   PC + 1
  //   Jump Register
  //   JUMP (PC + iMM)
  //   PC + 1
  //   PC + Imm
  //   opcode
  //   Branch On Zero Register
  //   Branch On Zero Imm
endmodule

module bankReg (
  input  [7:0] WB,
  input  WE,
  input  [1:0] ra,
  input  [1:0] rb,
  input  clk,
  output [7:0] out_6,
  output [7:0] out_7
);

  wire reg1, reg2, reg3, reg4;
  wire [7:0] register_1_q, register_2_q, register_3_q, register_4_q;

  Demultiplexer #(.select(2)) demultiplexer_1 (.out0(reg1), .out1(reg2), .out2(reg3), .out3(reg4), .in(WE), .sel(ra));
  Register register_1 (.D(WB), .en(reg1), .clk(clk), .Q(register_1_q));  // open: clr
  Register register_2 (.D(WB), .en(reg2), .clk(clk), .Q(register_2_q));  // open: clr
  Register register_3 (.D(WB), .en(reg3), .clk(clk), .Q(register_3_q));  // open: clr
  Register register_4 (.D(WB), .en(reg4), .clk(clk), .Q(register_4_q));  // open: clr
  Multiplexer #(.select(2), .width(8)) multiplexer_1 (
    .in0(register_1_q), .in1(register_2_q), .in2(register_3_q), .in3(register_4_q), .out(out_6), .sel(ra));
  Multiplexer #(.select(2), .width(8)) multiplexer_2 (
    .in0(register_1_q), .in1(register_2_q), .in2(register_3_q), .in3(register_4_q), .out(out_7), .sel(rb));
endmodule

module ula (
  input  [7:0] a,
  input  [7:0] b,
  input  [2:0] sel,
  input  [3:0] Imm,
  input  CntrHL,
  output [7:0] s
);

  wire [7:0] adder_1_out, and_1_out, deslocdir_1_s, deslocesq_1_s, move_1_s, not_1_out, or_1_out,
       subtractor_1_out;

  Adder adder_1 (.a(a), .b(b), .out(adder_1_out));  // open: cin, cout
  Subtractor subtractor_1 (.a(a), .b(b), .out(subtractor_1_out));  // open: bin, bout
  assign and_1_out = a & b;  // AND_Gate and_1, 8 bits wide
  assign or_1_out = a | b;  // OR_Gate or_1, 8 bits wide
  assign not_1_out = ~b;  // NOT_Gate not_1, 8 bits wide
  deslocDir deslocdir_1 (.regA(a), .regB(b), .s(deslocdir_1_s));
  deslocEsq deslocesq_1 (.regA(a), .regB(b), .s(deslocesq_1_s));
  move move_1 (.regA(a), .imm(Imm), .ctrl(CntrHL), .s(move_1_s));
  Multiplexer #(.select(3), .width(8)) multiplexer_1 (
    .in0(adder_1_out), .in1(subtractor_1_out), .in2(and_1_out), .in3(or_1_out), .in4(not_1_out),
    .in5(deslocdir_1_s), .in6(deslocesq_1_s), .in7(move_1_s), .out(s), .sel(sel));
endmodule

module deslocDir (
  input  [7:0] regA,
  input  [7:0] regB,
  output [7:0] s
);

  wire or_1_out;
  wire [7:0] shifter_1_out;

  or or_1 (or_1_out, regB[3], regB[4], regB[5], regB[6], regB[7]);
  Shifter #(.shift("lr")) shifter_1 (.in(regA), .\dist (regB[2:0]), .out(shifter_1_out));
  Multiplexer #(.width(8)) multiplexer_1 (.in0(shifter_1_out), .in1({8{1'b0}}), .out(s), .sel(or_1_out));
endmodule

module deslocEsq (
  input  [7:0] regA,
  input  [7:0] regB,
  output [7:0] s
);

  wire or_1_out;
  wire [7:0] shifter_1_out;

  or or_1 (or_1_out, regB[3], regB[4], regB[5], regB[6], regB[7]);
  Shifter shifter_1 (.in(regA), .\dist (regB[2:0]), .out(shifter_1_out));
  Multiplexer #(.width(8)) multiplexer_1 (.in0(shifter_1_out), .in1({8{1'b0}}), .out(s), .sel(or_1_out));
endmodule

module move (
  input  [7:0] regA,
  input  [3:0] imm,
  input  ctrl,
  output [7:0] s
);

  Multiplexer #(.width(8)) multiplexer_1 (.in0({imm, regA[3:0]}), .in1({regA[7:4], imm}), .out(s), .sel(ctrl));
endmodule
